// Logisim project ula.circ as structural Verilog: 1 circuit, main circuit main
// ULA
module main (
  input  [9:0] \Código ,
  output [3:0] \SAÍDA 
);

  // MULTIPLICADOR multiplicador_1: pin names not known
  // COMPARADOR comparador_1: pin names not known; wires that end beside it: \Código [3:0]
  mux_4_1__4_bits__main main_1 (.S(\Código [9:8]));  // open: A, B, C, D, OUT

  // Notes on the sheet:
  //   Opcodes - Operação:
  //   00 - ADD - 00
  //   01  - SUB - 01
  //   02 - MULT - 10
  //   03 - COMP - 11
  //   Estrutura Código:
  //   <opcode(2)> - imediato(4) - imediato(4)
endmodule
