// Logisim project AE_02_2025.circ as structural Verilog: 1 circuit, main circuit main
module main (
  input  RESET,
  output EN_PC,
  output [1:0] SEL_0,
  output [3:0] Output,
  output [1:0] SEL_1,
  output Op_FSM,
  output SEL_2
);

  wire and_1_out, and_2_out, and_3_out, and_4_out, and_5_out, and_6_out, and_7_out, and_8_out, and_9_out,
       and_10_out, clock_1_out, not_1_out, or_4_out, or_6_out, or_7_out, or_8_out, ST0_q, ST0_qn, ST1_q,
       ST1_qn, ST2_q, ST2_qn;
  wire [3:0] counter_1_q, multiplexer_1_out, multiplexer_2_out, multiplier_1_out, Reg_MULT_q, Reg_SUB_q,
       subtractor_1_out;
  wire [7:0] ram_1_data;

  Clock clock_1 (.out(clock_1_out));
  Counter #(.width(4), .max('hf)) counter_1 (
    .count(EN_PC), .Q(counter_1_q), .clk(clock_1_out), .clr(RESET));  // open: load, D, carry
  or or_1 (EN_PC, and_1_out, and_2_out);
  RAM #(.addrWidth(4), .dataWidth(9)) ram_1 (
    .addr(counter_1_q), .data({Op_FSM, ram_1_data}));  // open: sel, clk, ld, clr
  and and_1 (and_1_out, ST2_q, ST0_q);
  or or_2 (SEL_2, and_1_out, ST1_q);
  and and_2 (and_2_out, ST0_q, ST1_q);
  or or_3 (SEL_1[0], and_4_out, or_4_out);
  or or_4 (or_4_out, ST1_q, ST0_qn);
  Multiplexer #(.select(2), .width(4), .enable("false")) multiplexer_1 (
    .in0(ram_1_data[3:0]), .in1(ram_1_data[7:4]), .in2(Reg_MULT_q), .in3(Reg_SUB_q), .out(multiplexer_1_out),
    .sel(SEL_0));
  Multiplexer #(.select(2), .width(4), .enable("false")) multiplexer_2 (
    .in0(ram_1_data[3:0]), .in1(ram_1_data[7:4]), .in2(Reg_MULT_q), .in3(Reg_SUB_q), .out(multiplexer_2_out),
    .sel({1'b0, SEL_1[0]}));
  and and_3 (and_3_out, ST2_q, ST0_q);
  or or_5 (SEL_0[1], and_3_out, ST1_q);
  and and_4 (and_4_out, ST2_qn, ST1_qn, ST0_q);
  xor xor_1 (SEL_0[0], ST2_q, ST0_q);
  Multiplier #(.width(4)) multiplier_1 (
    .a(multiplexer_1_out), .b(multiplexer_2_out), .out(multiplier_1_out));  // open: cin, cout
  Subtractor #(.width(4)) subtractor_1 (
    .a(multiplexer_1_out), .b(multiplexer_2_out), .out(subtractor_1_out));  // open: bin, bout
  or or_6 (or_6_out, ST2_q, and_5_out);
  or or_7 (or_7_out, and_6_out, and_7_out);
  or or_8 (or_8_out, and_8_out, and_9_out, and_10_out);
  Register #(.width(4)) Reg_MULT (.D(multiplier_1_out), .Q(Reg_MULT_q), .clk(clock_1_out), .clr(RESET));  // open: en
  Register #(.width(4)) Reg_SUB (.D(subtractor_1_out), .Q(Reg_SUB_q), .clk(clock_1_out), .clr(RESET));  // open: en
  and and_5 (and_5_out, ST1_qn, Op_FSM, ST0_qn);
  and and_6 (and_6_out, ST2_qn, ST1_qn, ST0_q);
  and and_7 (and_7_out, ST1_q, ST0_qn);
  and and_8 (and_8_out, ST1_q, ST0_qn);
  and and_9 (and_9_out, ST0_qn, not_1_out);
  and and_10 (and_10_out, ST2_q, ST0_qn);
  Multiplexer #(.width(4), .enable("false")) multiplexer_3 (
    .in0(Reg_MULT_q), .in1(Reg_SUB_q), .out(Output), .sel(SEL_2));
  not not_1 (not_1_out, Op_FSM);
  D_Flip_Flop ST2 (.clk(clock_1_out), .D(or_6_out), .Q(ST2_q), .Qn(ST2_qn), .reset(RESET));  // open: preset, en
  D_Flip_Flop ST1 (.clk(clock_1_out), .D(or_7_out), .Q(ST1_q), .Qn(ST1_qn), .reset(RESET));  // open: preset, en
  D_Flip_Flop ST0 (.clk(clock_1_out), .D(or_8_out), .Q(ST0_q), .Qn(ST0_qn), .reset(RESET));  // open: preset, en

  assign SEL_1[1] = 1'b0;

  // Notes on the sheet:
  //   OP_FSM,A,B
  //   b
endmodule
